# Fritzing sketch encoders (saved by Fritzing 1.0.2b)
breadboards: 1

parts:
  Part3 = Arduino Uno (Rev3) - ICSP
  Enc1 = shaft encoder
  Enc2 = shaft encoder

nets:
  N1: Part3.D2, Enc2.OUT
  GND: Part3.GND, Enc1.GND, Enc2.GND
  VCC: Enc1.VCC, Enc2.VCC
